# Fritzing sketch rng_back (saved by Fritzing 0.9.4)
perfboards: 1

parts:
  J1 = male pin header, 7 pins [form="♂ (male)"]
  IC1 = IC, DIP package, 28 pins [chip_label=TLC5940NT]
  Part1 = Arduino Nano (Rev3.0)
  R1 = Resistor [tolerance=±5% resistance=220 package=THT]
  IC2 = IC, DIP package, 14 pins [chip_label=MCP4922]
  IC3 = IC, DIP package, 8 pins [chip_label=TL072]  # not connected
  J2 = male pin header, 9 pins [form="♂ (male)"]

nets:
  N1: J1.pin1, IC1.pin28
  N2: J1.pin2, IC1.pin1
  N3: J1.pin3, IC1.pin2
  N4: J1.pin4, IC1.pin3
  N5: J1.pin5, IC1.pin4
  N6: J1.pin6, IC1.pin5
  N7: J1.pin7, IC1.pin6
  N8: IC1.pin18, Part1.D3
  N9: IC1.pin20, R1.Pin_1
  N10: IC1.pin21, Part1.A6
  N11: IC1.pin22, IC1.pin27, Part1.GND, R1.Pin_0, J2.pin1
  N12: IC1.pin23, Part1.D12/MISO
  N13: IC1.pin24, Part1.D9
  N14: IC1.pin25, Part1.D13/SCK
  N15: IC1.pin26, Part1.D11/MOSI
  N16: Part1.5V, J2.pin2
  N17: Part1.A5, J2.pin4
  N18: Part1.A4, J2.pin5
  N19: Part1.A3, J2.pin6
  N20: Part1.A2, J2.pin7
  N21: Part1.A1, J2.pin8
  N22: Part1.A0, J2.pin9
  N23: IC2.pin9, IC2.pin11, IC2.pin13
