# Fritzing sketch sequencer_pcb_back (saved by Fritzing 0.9.4)
perfboards: 1

parts:
  J7 = female pin header, 4 pins [form="♀ (female)"]
  J8 = female pin header, 10 pins [form="♀ (female)"]
  J9 = female pin header, 4 pins [form="♀ (female)"]
  J10 = female pin header, 4 pins [form="♀ (female)"]
  J11 = female pin header, 4 pins [form="♀ (female)"]
  J15 = female pin header, 4 pins [form="♀ (female)"]
  IC1 = IC, DIP package, 16 pins [chip_label=CD4051be]
  IC2 = IC, DIP package, 16 pins [chip_label=CD4051be]
  J17 = female pin header, 5 pins [form="♀ (female)"]
  IC3 = IC, DIP package, 28 pins [chip_label=MCP23S17]
  J18 = female pin header, 2 pins [form="♀ (female)"]
  Part1 = Arduino Nano (Rev3.0)
  IC4 = IC, DIP package, 14 pins [chip_label=MCP4922]
  IC5 = IC, DIP package, 14 pins [chip_label=MCP4922]
  IC6 = IC, DIP package, 28 pins [chip_label=MCP23S17]
  R1 = Resistor [tolerance=±5% resistance=1k package=THT]
  R2 = Resistor [tolerance=±5% resistance=1k package=THT]
  R3 = Resistor [tolerance=±5% resistance=1k package=THT]
  R4 = Resistor [tolerance=±5% resistance=1k package=THT]
  J14 = female pin header, 6 pins [form="♀ (female)"]
  J16 = female pin header, 7 pins [form="♀ (female)"]
  R5 = Resistor [tolerance=±5% resistance=100k package=THT]
  R6 = Resistor [tolerance=±5% resistance=100k package=THT]
  R7 = Resistor [tolerance=±5% resistance=100k package=THT]
  R8 = Resistor [tolerance=±5% resistance=100k package=THT]
  R9 = Resistor [tolerance=±5% resistance=100k package=THT]
  R10 = Resistor [tolerance=±5% resistance=100k package=THT]
  R11 = Resistor [tolerance=±5% resistance=100k package=THT]
  R12 = Resistor [tolerance=±5% resistance=100k package=THT]
  Q1 = NPN-Transistor [package="TO92 [THT]"]
  Q2 = NPN-Transistor [package="TO92 [THT]"]
  Q3 = NPN-Transistor [package="TO92 [THT]"]
  R13 = Resistor [tolerance=±5% resistance=100k package=THT]
  R14 = Resistor [tolerance=±5% resistance=100k package=THT]
  Q4 = NPN-Transistor [package="TO92 [THT]"]
  Q5 = NPN-Transistor [package="TO92 [THT]"]
  R15 = Resistor [tolerance=±5% resistance=100k package=THT]
  R16 = Resistor [tolerance=±5% resistance=100k package=THT]
  R17 = Resistor [tolerance=±5% resistance=100k package=THT]
  R18 = Resistor [tolerance=±5% resistance=100k package=THT]
  R19 = Resistor [tolerance=±5% resistance=100k package=THT]
  R20 = Resistor [tolerance=±5% resistance=100k package=THT]
  R21 = Resistor [tolerance=±5% resistance=100k package=THT]
  R22 = Resistor [tolerance=±5% resistance=100k package=THT]
  Q6 = NPN-Transistor [package="TO92 [THT]"]
  Q7 = NPN-Transistor [package="TO92 [THT]"]
  Q8 = NPN-Transistor [package="TO92 [THT]"]
  Q9 = NPN-Transistor [package="TO92 [THT]"]
  J19 = shrouded pin header, 16 pins [form="♂ (shrouded male)"]

nets:
  N1: J7.pin1, R18.Pin_0
  N2: J7.pin2, R17.Pin_0
  N3: J7.pin3, R16.Pin_0
  N4: J7.pin4, R15.Pin_0
  N5: J8.pin1, IC1.pin8, IC2.pin8, IC3.pin10, IC3.pin15, IC3.pin16, IC3.pin17, Part1.GND, IC6.pin10, IC6.pin16, IC6.pin17
  N6: J8.pin2, IC6.pin8
  N7: J8.pin3, IC6.pin4
  N8: J8.pin4, IC6.pin7
  N9: J8.pin5, IC6.pin3
  N10: J8.pin6, IC6.pin6
  N11: J8.pin7, IC6.pin2
  N12: J8.pin8, IC6.pin5
  N13: J8.pin9, IC6.pin1
  N14: J8.pin10, IC1.pin16, IC2.pin16, IC3.pin9, IC3.pin18, Part1.5V, IC4.pin1, IC4.pin9, IC4.pin11, IC4.pin13, IC5.pin1, IC5.pin9, IC5.pin11, IC5.pin13, IC6.pin9, IC6.pin15, IC6.pin18, J19.pin6, J19.pin11
  N15: J9.pin1, IC4.pin14
  N16: J9.pin2, IC4.pin10
  N17: J9.pin3, IC5.pin14
  N18: J9.pin4, IC5.pin10
  N19: J10.pin1, R4.Pin_0
  N20: J10.pin2, R3.Pin_0
  N21: J10.pin3, R2.Pin_0
  N22: J10.pin4, R1.Pin_0
  N23: J11.pin1, IC1.pin15
  N24: J11.pin2, IC1.pin14
  N25: J11.pin3, IC1.pin13
  N26: J11.pin4, IC1.pin12
  N27: J15.pin1, IC2.pin15
  N28: J15.pin2, IC2.pin14
  N29: J15.pin3, IC2.pin13
  N30: J15.pin4, IC2.pin12
  N31: IC1.pin1, J14.pin5
  N32: IC1.pin2, J14.pin4
  N33: IC1.pin3, Part1.A7
  N34: IC1.pin4, J14.pin3
  N35: IC1.pin5, J14.pin2
  N36: IC1.pin9, IC2.pin9, Part1.D4
  N37: IC1.pin10, IC2.pin10, Part1.D5
  N38: IC1.pin11, IC2.pin11, Part1.D6
  N39: IC2.pin1, J16.pin5
  N40: IC2.pin2, J16.pin4
  N41: IC2.pin3, Part1.A6
  N42: IC2.pin4, J16.pin3
  N43: IC2.pin5, J16.pin2
  N44: J17.pin1, IC3.pin6
  N45: J17.pin2, IC3.pin5
  N46: J17.pin3, IC3.pin4
  N47: J17.pin4, IC3.pin3
  N48: J17.pin5, IC3.pin2
  N49: IC3.pin1, Q2.C
  N50: IC3.pin7, J18.pin1
  N51: IC3.pin8, J18.pin2
  N52: IC3.pin11, Part1.D7
  N53: IC3.pin12, Part1.D13/SCK, IC4.pin4, IC5.pin4, IC6.pin12
  N54: IC3.pin13, Part1.D11/MOSI, IC4.pin5, IC5.pin5, IC6.pin13
  N55: IC3.pin14, Part1.D12/MISO, IC6.pin14
  N56: IC3.pin19, Part1.D2
  N57: IC3.pin20, Part1.D3
  N58: IC3.pin21, Q3.C
  N59: IC3.pin22, Q1.C
  N60: IC3.pin23, Q4.C
  N61: IC3.pin24, Q5.C
  N62: IC3.pin25, Q6.C
  N63: IC3.pin26, Q7.C
  N64: IC3.pin27, Q8.C
  N65: IC3.pin28, Q9.C
  N66: Part1.D8, IC6.pin11
  N67: Part1.D9, IC4.pin3
  N68: Part1.D10, IC5.pin3
  N69: Part1.A5, R4.Pin_1
  N70: Part1.A4, R3.Pin_1
  N71: Part1.A3, R2.Pin_1
  N72: Part1.A2, R1.Pin_1
  N73: IC4.pin8, IC4.pin12, IC5.pin8, IC5.pin12, J19.pin2, J19.pin3, J19.pin4, J19.pin13, J19.pin14, J19.pin15
  N74: J14.pin1, R8.Pin_0
  N75: J14.pin6, R7.Pin_0
  N76: J16.pin1, R6.Pin_0
  N77: J16.pin6, R5.Pin_0
  N78: J16.pin7, R11.Pin_0
  N79: R5.Pin_1, R10.Pin_1, Q3.B
  N80: R6.Pin_1, R9.Pin_1, Q1.B
  N81: R7.Pin_1, R13.Pin_0, Q4.B
  N82: R8.Pin_1, R14.Pin_0, Q5.B
  N83: R9.Pin_0, Q1.E
  N84: R10.Pin_0, Q3.E
  N85: R11.Pin_1, R12.Pin_1, Q2.B
  N86: R12.Pin_0, Q2.E
  N87: R13.Pin_1, Q4.E
  N88: R14.Pin_1, Q5.E
  N89: R15.Pin_1, R19.Pin_1, Q9.B
  N90: R16.Pin_1, R20.Pin_1, Q8.B
  N91: R17.Pin_1, R21.Pin_1, Q7.B
  N92: R18.Pin_1, R22.Pin_1, Q6.B
  N93: R19.Pin_0, R20.Pin_0, R21.Pin_0, R22.Pin_0, Q6.E, Q7.E, Q8.E, Q9.E
